# Fritzing sketch PCBv0.7.1 (saved by Fritzing 0.9.4)
circuit board: 6.53631cm x 5.1779cm
breadboards: 1

parts:
  LCD1 = LCD screen
  v0_7_1_Station_C°_et_Hygro = Arduino Uno (Rev3)
  R2 = Resistor [tolerance=±5% resistance=10k package=THT]
  R3 = Resistor [tolerance=±5% resistance=220 package=THT]
  R4 = Rotary Potentiometer (Large) [maximum_resistance=10kΩ package=THT]
  DHT23 = DHT22 Humidity and Temperature Sensor
  S2 = Pushbutton [package=THT]

nets:
  GND: LCD1.VSS, LCD1.R/W, v0_7_1_Station_C°_et_Hygro.GND, R4.leg2, DHT23.GND, S2.leg0
  VDD: LCD1.VDD, v0_7_1_Station_C°_et_Hygro.5V, R2.Pin_1, R3.Pin_0, R4.leg1, DHT23.NULL
  N1: LCD1.V0, R4.wiper
  N2: LCD1.RS, v0_7_1_Station_C°_et_Hygro.D3_PWM
  N3: LCD1.E, v0_7_1_Station_C°_et_Hygro.D4
  N4: LCD1.DB4, v0_7_1_Station_C°_et_Hygro.D5_PWM
  N5: LCD1.DB5, v0_7_1_Station_C°_et_Hygro.D6_PWM
  N6: LCD1.DB6, v0_7_1_Station_C°_et_Hygro.D7
  N7: LCD1.DB7, v0_7_1_Station_C°_et_Hygro.D8
  N8: LCD1.LED+, R3.Pin_1
  N9: LCD1.LED-, v0_7_1_Station_C°_et_Hygro.D9_PWM, S2.leg1
  N10: v0_7_1_Station_C°_et_Hygro.D2, R2.Pin_0, DHT23.DATA

notes:
  Pour des raisons de modèle DHTs il faut réjauster les cablages selon le modèle.
