# Fritzing sketch Projet Station Sketch (saved by Fritzing 0.9.4)
circuit board: 6.05993cm x 5.34714cm
breadboards: 1

parts:
  DHT22 = DHT22 Humidity and Temperature Sensor
  Erreur = LED - 5mm [color="Red (633nm)" package="5 mm [THT]"]
  Enregistre = LED - 5mm [color="Green (555nm)" package="5 mm [THT]"]
  lit = LED - 5mm [color="Yellow (595nm)" package="5 mm [THT]"]
  R2 = Resistor [tolerance=±5% resistance=220 package=THT]
  R3 = Resistor [tolerance=±5% resistance=220 package=THT]
  R4 = Resistor [tolerance=±5% resistance=220 package=THT]
  v0_6_0_Station_C°_et_Hygro = Arduino Uno (Rev3)
  R1 = Resistor [tolerance=±5% resistance=10k package=THT]

nets:
  VDD: DHT22.VDD, v0_6_0_Station_C°_et_Hygro.5V, R1.Pin_1
  N1: DHT22.DATA, v0_6_0_Station_C°_et_Hygro.D2, R1.Pin_0
  GND: DHT22.GND, R2.Pin_1, R3.Pin_1, R4.Pin_1, v0_6_0_Station_C°_et_Hygro.GND
  N2: Erreur.cathode, v0_6_0_Station_C°_et_Hygro.D5_PWM
  N3: Erreur.anode, R2.Pin_0
  N4: Enregistre.cathode, v0_6_0_Station_C°_et_Hygro.D6_PWM
  N5: Enregistre.anode, R3.Pin_0
  N6: lit.cathode, v0_6_0_Station_C°_et_Hygro.D7
  N7: lit.anode, R4.Pin_0
